# Fritzing sketch 6502_computer (saved by Fritzing 0.9.3b)
breadboards: 6

parts:
  IC1 = 74HC08 Logic AND Gate [part_number=74HC08 package="DIP (Dual Inline) [THT]"]
  IC2 = IC, DIP package, 20 pins [chip_label=74HCT688E]
  IC3 = IC, DIP package, 20 pins [chip_label=74HCT688E]
  IC4 = IC, DIP package, 20 pins [chip_label=74HCT688E]
  IC5 = 74HC08 Logic AND Gate [part_number=74HC08 package="DIP (Dual Inline) [THT]"]  # not connected
  Q1 = NPN-Transistor [package="TO92 [THT]"]  # not connected
  IC6 = IC, DIP package, 16 pins [chip_label=74LS161A]
  Q2 = NPN-Transistor [package="TO92 [THT]"]  # not connected
  U3 = 74HC595 [package="DIP16 [THT]"]
  U4 = 74HC595 [package="DIP16 [THT]"]  # not connected
  IC7 = IC, DIP package, 20 pins [chip_label=74LS244AN]
  U5 = SWITCH_SPDT [package=kps-1290]  # not connected
  IC8 = IC, DIP package, 40 pins [chip_label="WDC 65C02"]
  U6 = SWITCH_SPDT [package=kps-1290]  # not connected
  IC9 = IC, DIP package, 14 pins [chip_label=74HC04]
  IC10 = IC, DIP package, 14 pins [chip_label=74HC04]  # not connected
  IC11 = Voltage Regulator [package=to220-igo]  # not connected
  XTAL1 = Crystal [frequency="1 MHz" package=THT]  # not connected
  IC12 = 74HC08 Logic AND Gate [part_number=74HC08 package="DIP (Dual Inline) [THT]"]  # not connected
  IC13 = IC, DIP package, 14 pins [chip_label=74HC04]  # not connected
  S1 = Pushbutton [package="[THT]"]
  IC14 = IC, DIP package, 28 pins [chip_label="28C256-15 EEPROM"]  # not connected
  IC15 = IC, DIP package, 14 pins [chip_label=74HC04]  # not connected
  IC16 = IC, DIP package, 28 pins [chip_label="CY7C199-35PC SRAM"]  # not connected
  U7 = SWITCH_SPDT [package=kps-1290]  # not connected
  IC17 = IC, DIP package, 14 pins [chip_label=74LS32]  # not connected
  IC18 = IC, DIP package, 14 pins [chip_label=74LS32]  # not connected
  IC19 = IC, DIP package, 14 pins [chip_label=74LS32]  # not connected
  IC20 = IC, DIP package, 14 pins [chip_label=74LS32]  # not connected
  U8 = SWITCH_SPDT [package=kps-1290]  # not connected
  U9 = 74HC595 [package="DIP16 [THT]"]  # not connected
  U10 = 74HC595 [package="DIP16 [THT]"]  # not connected
  U11 = 74HC595 [package="DIP16 [THT]"]  # not connected
  U12 = SWITCH_SPDT [package=kps-1290]  # not connected
  U13 = SWITCH_SPDT [package=kps-1290]  # not connected
  U14 = SWITCH_SPDT [package=kps-1290]  # not connected
  U15 = SWITCH_SPDT [package=kps-1290]  # not connected
  U16 = SWITCH_SPDT [package=kps-1290]  # not connected
  U17 = SWITCH_SPDT [package=kps-1290]  # not connected
  U18 = SWITCH_SPDT [package=kps-1290]  # not connected
  U19 = SWITCH_SPDT [package=kps-1290]  # not connected
  U20 = SWITCH_SPDT [package=kps-1290]  # not connected
  U21 = SWITCH_SPDT [package=kps-1290]  # not connected
  IC21 = IC, DIP package, 14 pins [chip_label=74HC04]
  U22 = POT [package=3362u]  # not connected
  LCD1 = LCD screen  # not connected
  U23 = mini DIN 6 Connector [package=mini-din6]
  C2 = Ceramic Capacitor [capacitance=0.1µF package="200 mil [THT, multilayer]"]
  C3 = Ceramic Capacitor [capacitance=0.1µF package="200 mil [THT, multilayer]"]
  C4 = Ceramic Capacitor [capacitance=0.1µF package="200 mil [THT, multilayer]"]
  C5 = Ceramic Capacitor [capacitance=0.1µF package="200 mil [THT, multilayer]"]
  C6 = Ceramic Capacitor [capacitance=0.1µF package="200 mil [THT, multilayer]"]

nets:
  N1: IC1.1A, IC9.pin2
  N2: IC1.1B, IC9.pin4
  N3: IC1.1Y, IC9.pin5
  N4: IC1.2A, IC2.pin17, IC8.pin25
  N5: IC1.2B, IC9.pin6
  N6: IC1.2Y, IC21.pin1
  N7: IC1.GND, IC2.pin1, IC2.pin10, IC3.pin1, IC3.pin5, IC3.pin7, IC3.pin10, IC4.pin1, IC4.pin9, IC4.pin10, IC7.pin10, IC9.pin7, U23.2, C2.0, C3.1, C5.1, C6.1
  N8: IC1.4Y, IC9.pin9
  N9: IC1.4A, IC9.pin10
  N10: IC1.4B, IC9.pin12
  N11: IC1.VCC, IC2.pin3, IC2.pin5, IC2.pin7, IC2.pin9, IC2.pin12, IC2.pin14, IC2.pin16, IC2.pin18, IC2.pin20, IC3.pin3, IC3.pin9, IC3.pin12, IC3.pin14, IC3.pin16, IC3.pin18, IC3.pin20, IC4.pin3, IC4.pin5, IC4.pin7, IC4.pin12, IC4.pin14, IC4.pin16, IC4.pin18, IC4.pin20, IC8.pin18, IC9.pin14, U23.1, C2.1, C4.0, C5.0
  N12: IC2.pin2, IC8.pin17
  N13: IC2.pin6, IC8.pin19
  N14: IC2.pin8, IC8.pin20
  N15: IC2.pin11, IC8.pin22
  N16: IC2.pin13, IC8.pin23
  N17: IC2.pin15, IC8.pin24
  N18: IC2.pin19, IC9.pin1, IC9.pin13
  N19: IC3.pin2, IC4.pin2
  N20: IC3.pin4, IC4.pin4
  N21: IC3.pin6, IC4.pin6
  N22: IC3.pin8, IC4.pin8
  N23: IC3.pin11, IC4.pin11
  N24: IC3.pin13, IC4.pin13
  N25: IC3.pin15, IC4.pin15
  N26: IC3.pin17, IC4.pin17
  N27: IC3.pin19, IC9.pin11
  N28: IC4.pin19, IC9.pin3
  N29: IC6.pin1, IC9.pin8
  N30: U3.DS, U23.5
  N31: S1.Pin_1, S1.Pin_2
  N32: S1.Pin_3, S1.Pin_4

notes:
  PS/2 Keyboard
  Data
  Clock
